# Fritzing sketch setup (saved by Fritzing 0.9.3b)

parts:
  BAT1 = Battery Holders [package=battery-aaa]
  BAT2 = Battery Holders [package=battery-aaa]
  NodeMCU_1_0_ESP8266-E12 = Adafruit HUZZAH ESP8266 Breakout
  BAT3 = Battery Holders [package=battery-aaa]
  J1 = Basic Force Sensing Resistor (FSR) [package=THT]

nets:
  N1: BAT1.-, NodeMCU_1_0_ESP8266-E12.GND, J1.pin_1
  N2: BAT1.+, BAT2.-
  N3: BAT2.+, BAT3.-
  N4: NodeMCU_1_0_ESP8266-E12.VBat, BAT3.+
  N5: NodeMCU_1_0_ESP8266-E12.A, J1.pin_0
